# Fritzing sketch ADC_rev2 (saved by Fritzing 1.0.0d)
breadboards: 1

parts:
  Part1 = Adafruit T-Cobbler Plus [part_number="Adafruit #1989 and #2028"]
  IC1 = MCP3008 8-channel 10-bit ADC [part_number=MCP3008]
  U1 = POT [knob_status=50% power=0.5W package=3362u]

nets:
  N1: Part1.+3.3V, IC1.no_name_yet#15, IC1.no_name_yet#16, U1.E
  N2: Part1.GND, IC1.no_name_yet#9, IC1.no_name_yet#14, U1.A
  N3: Part1.MOSI, IC1.no_name_yet#11
  N4: Part1.MISO, IC1.no_name_yet#12
  N5: Part1.SCLK, IC1.no_name_yet#13
  N6: Part1.CE0, IC1.no_name_yet#10
  N7: IC1.no_name_yet#1, U1.S

custom parts:
  Adafruit T-Cobbler Plus: The Raspberry Pi has landed on the Maker World like a 40-GPIO pinned, quad-USB ported, credit card sized bomb of DIY joy. And while you can use most of our great Model B accessories by hooking up our downgrade cable, its probably a good time to upgrade your set up and accessorize using all of the 40 pins. That's why we now carry the Assembled Adafruit Pi T-Cobbler Plus - Breakout + Cable for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
