# Fritzing sketch HalfAdder_rev2 (saved by Fritzing 1.0.0d)
breadboards: 1

parts:
  Part1 = Adafruit T-Cobbler Plus [part_number="Adafruit #1989 and #2028"]
  IC3 = IC, DIP package, 14 pins [chip_label=7486]
  IC4 = IC, DIP package, 14 pins [chip_label=7408]

nets:
  N1: Part1.+3.3V, IC3.pin14, IC4.pin14
  N2: Part1.GND, IC3.pin7, IC4.pin7
  N3: Part1.GPIO27, IC3.pin1, IC4.pin1
  N4: Part1.GPIO22, IC3.pin2, IC4.pin2
  N5: Part1.GPIO23, IC3.pin3
  N6: Part1.GPIO24, IC4.pin3

custom parts:
  Adafruit T-Cobbler Plus: The Raspberry Pi has landed on the Maker World like a 40-GPIO pinned, quad-USB ported, credit card sized bomb of DIY joy. And while you can use most of our great Model B accessories by hooking up our downgrade cable, its probably a good time to upgrade your set up and accessorize using all of the 40 pins. That's why we now carry the Assembled Adafruit Pi T-Cobbler Plus - Breakout + Cable for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
