# Fritzing sketch SR_Latch_with_NOR_gates (saved by Fritzing 1.0.0d)
breadboards: 1

parts:
  Part1 = Adafruit T-Cobbler Plus [part_number="Adafruit #1989 and #2028"]
  LED1 = LED - 5mm [color="Red (633nm)" current=0.030 package="5 mm [THT]"]
  R1 = Resistor [tolerance=±5% power=0.25 resistance=470k package=THT]
  S1 = Pushbutton [package="[THT]"]
  R2 = Resistor [tolerance=±5% power=0.25 resistance=1k package=THT]
  R3 = Resistor [tolerance=±5% power=0.25 resistance=1k package=THT]
  S2 = Pushbutton [package="[THT]"]
  7404 = DIP - 14 pins [chip_label=7402 package="DIP (Dual Inline) [THT]"]

nets:
  GND: Part1.GND, R1.Pin_1, R2.Pin_1, R3.Pin_1, 7404.GND
  N1: Part1.+3.3V_2, S1.Pin_3, S1.Pin_4, S2.Pin_3, S2.Pin_4, 7404.Vcc
  N2: LED1.cathode, R1.Pin_0
  N3: LED1.anode, 7404.5Y, 7404.6Y
  N4: S1.Pin_1, S1.Pin_2, R3.Pin_0, 7404.4Y
  N5: R2.Pin_0, S2.Pin_1, S2.Pin_2, 7404.5A
  N6: 7404.4A, 7404.6A

custom parts:
  Adafruit T-Cobbler Plus: The Raspberry Pi has landed on the Maker World like a 40-GPIO pinned, quad-USB ported, credit card sized bomb of DIY joy. And while you can use most of our great Model B accessories by hooking up our downgrade cable, its probably a good time to upgrade your set up and accessorize using all of the 40 pins. That's why we now carry the Assembled Adafruit Pi T-Cobbler Plus - Breakout + Cable for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
  DIP - 14 pins: 7404 Hex Inverter
