# Fritzing sketch SR_Latch_with_NOR_gates_with_RPi (saved by Fritzing 1.0.0d)
breadboards: 1

parts:
  Part1 = Adafruit T-Cobbler Plus [part_number="Adafruit #1989 and #2028"]
  LED1 = LED - 5mm [color="Red (633nm)" current=0.030 package="5 mm [THT]"]
  R1 = Resistor [tolerance=±5% power=0.25 resistance=470k package=THT]
  7404 = DIP - 14 pins [chip_label=7402 package="DIP (Dual Inline) [THT]"]

nets:
  GND: Part1.GND, R1.Pin_1, 7404.GND
  N1: Part1.+3.3V_2, 7404.Vcc
  N2: Part1.GPIO26, LED1.anode, 7404.5Y, 7404.6Y
  N3: Part1.GPIO16, 7404.5A
  N4: Part1.GPIO20, 7404.4Y
  N5: LED1.cathode, R1.Pin_0
  N6: 7404.4A, 7404.6A

custom parts:
  Adafruit T-Cobbler Plus: The Raspberry Pi has landed on the Maker World like a 40-GPIO pinned, quad-USB ported, credit card sized bomb of DIY joy. And while you can use most of our great Model B accessories by hooking up our downgrade cable, its probably a good time to upgrade your set up and accessorize using all of the 40 pins. That's why we now carry the Assembled Adafruit Pi T-Cobbler Plus - Breakout + Cable for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
  DIP - 14 pins: 7404 Hex Inverter
