# Fritzing sketch circuit_servo (saved by Fritzing 1.0.0d)
breadboards: 1

parts:
  Part1 = Adafruit T-Cobbler Plus [part_number="Adafruit #1989 and #2028"]
  J1 = Basic Servo

nets:
  +3.3V: Part1.+3.3V, J1.vcc
  GND: Part1.GND, J1.gnd
  N1: Part1.GPIO17, J1.pulse

custom parts:
  Adafruit T-Cobbler Plus: The Raspberry Pi has landed on the Maker World like a 40-GPIO pinned, quad-USB ported, credit card sized bomb of DIY joy. And while you can use most of our great Model B accessories by hooking up our downgrade cable, its probably a good time to upgrade your set up and accessorize using all of the 40 pins. That's why we now carry the Assembled Adafruit Pi T-Cobbler Plus - Breakout + Cable for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
